# Fritzing sketch layout (saved by Fritzing 0.9.3b)
breadboards: 1

parts:
  元件1 = Arduino Mega 2560 (Rev3)
  hc-sr1 = hc-sr04
  IRL = Infrared Proximity Sensor
  DHT11_1 = DHT11 module
  元件2 = RFID-RC522-v2
  IRR = Infrared Proximity Sensor
  元件3 = Triple Axis Accelerometer Breakout - ADXL345
  S1 = Pololu QTR-8 Reflectabce Sensor array [package=THT]
  ML = DC Motor
  MR = DC Motor
  Q1 = TRANSISTOR_NPN [package=to-92-ammo]  # not connected

nets:
  N1: 元件1.A0, 元件2.RST
  N2: 元件1.D13_PWM, 元件2.SCK
  N3: 元件1.D12_PWM, 元件2.MISO
  N4: 元件1.D11_PWM, 元件2.MOSI
  N5: 元件1.D10_PWM, 元件2.SDA
  N6: 元件1.D9_PWM, ML.pin_1
  N7: 元件1.D8_PWM, MR.pin_1
  3V3: 元件1.3V3, 元件2.3.3V
  VCC: 元件1.5V, hc-sr1.VCC, IRL.Vcc, DHT11_1.VCC, IRR.Vcc, 元件3.VCC, S1.pin14, S1.pin22
  GND: 元件1.GND, hc-sr1.GND, IRL.GND, DHT11_1.GND, 元件2.GND, IRR.GND, 元件3.GND, S1.pin15, S1.pin21, ML.pin_2, MR.pin_2
  N8: 元件1.D2_PWM, hc-sr1.Trig
  N9: 元件1.D3_PWM, hc-sr1.Echo
  N10: 元件1.D4_PWM, IRL.Vout
  N11: 元件1.D5_PWM, IRR.Vout
  N12: 元件1.D6_PWM, DHT11_1.DATA
  N13: 元件1.D31, S1.pin12
  N14: 元件1.D32, S1.pin11
  N15: 元件1.D33, S1.pin10
  N16: 元件1.D34, S1.pin9
  N17: 元件1.D35, S1.pin8
  N18: 元件1.D36, S1.pin7
  N19: 元件1.D37, S1.pin4, S1.pin6
  N20: 元件1.D38, S1.pin3, S1.pin5
  N21: 元件1.D42, 元件3.INT1
  N22: 元件1.D43, 元件3.INT2

custom parts:
  DHT11 module: DHT11 black pcb module
  RFID-RC522-v2: A simple China made RFID-RC522 Reader; do check the pin labels, as this is a MFRC522 based clone.
