# Fritzing sketch 專題_瓦斯偵測 (saved by Fritzing 0.9.3b)
circuit board: 11.0162cm x 9.78749cm
breadboards: 1

parts:
  ESP32 = ESP32S-HiLetgo [part_number=ESP32S-HiLetgo]
  7_Segment = 7 Segment Display
  Buzzer = Piezo Speaker
  MQ = MQ-7 breakout
  Servo = Basic Servo

nets:
  N1: ESP32.3.3, Servo.vcc
  N2: ESP32.GPIO36, MQ.AO
  N3: ESP32.GPIO33, Buzzer.pin2
  N4: ESP32.GPIO26, Servo.pulse
  GND: ESP32.GND, ESP32.GPIO0, ESP32.GPIO16, ESP32.GPIO18, ESP32.GPIO21, ESP32.GPIO23, 7_Segment.common_cathode#3, 7_Segment.common_cathode#5, 7_Segment.common_cathode#11, 7_Segment.Segment_G, 7_Segment.common_cathode#16, Buzzer.pin1, MQ.GND, Servo.gnd
  VIN: ESP32.VIN, MQ.VCC
  N5: ESP32.GPIO8, ESP32.GPIO15, 7_Segment.Segment_A
  N6: ESP32.GPIO2, 7_Segment.Segment_F
  N7: ESP32.GPIO4, 7_Segment.Segment_E
  N8: ESP32.GPIO17, 7_Segment.Segment_DP
  N9: ESP32.GPIO5, 7_Segment.Segment_D
  N10: ESP32.GPIO19, 7_Segment.common_cathode#12
  N11: ESP32.GPIO1, ESP32.GPIO22, 7_Segment.Segment_B

notes:
  7段顯示器示意圖
  詳細接線請詳見
  github.com/jason19970210/Arduino/blob/master/學校專題_瓦斯偵測/Combine_V3/Combine_V3.ino
  瓦斯偵測器 MQ-2 (此處以 MQ-7模型代替)
  詳細接線請詳見
  github.com/jason19970210/Arduino/blob/master/學校專題_瓦斯偵測/Combine_V3/Combine_V3.ino

custom parts:
  ESP32S-HiLetgo: HiLetgo ESP-WROOM-32 ESP32 ESP-32S Development Board 2.4GHz Dual-Mode WiFi + Bluetooth Dual Cores Microcontroller The ESP32 integrated with Antenna switches, RF Balun, power amplifiers, low-noise amplifiers, filters, and management modules, and the entire solution occupies the least area of PCB. 2.4 GHz Wi-Fi plus Bluetooth dual-mode chip, with TSMC Ultra-low power consumption 40nm technology,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
  MQ-7 breakout: SKU: 101282
